// Logisim project calculator.circ as structural Verilog: 23 circuits, main circuit main
module main (
  output [31:0] From__t9,
  output [31:0] to__t9
);

  wire _0_out, _1_out, _2_out, _3_out, _4_out, _5_out, _6_out, _7_out, _8_out, _9_out, button_2_out,
       button_3_out, button_4_out, button_5_out, button_out, C_out, keypad_controller_1_write;
  wire [2:0] lcd_controller_1__7_segment_0_2, lcd_controller_1__7_segment_2_2,
       lcd_controller_1__7_segment_3_2, lcd_controller_1__7_segment_4_2, lcd_controller_1__7_segment_6_2,
       lcd_controller_1__7_segment_7_2, lcd_controller_1_minus_2;
  wire [3:0] lcd_controller_1__7_segment_0, lcd_controller_1__7_segment_2, lcd_controller_1__7_segment_3,
       lcd_controller_1__7_segment_4, lcd_controller_1__7_segment_6, lcd_controller_1__7_segment_7,
       lcd_controller_1_minus;
  wire [6:0] lcd_controller_1__7_segment_1, lcd_controller_1__7_segment_5, lcd_controller_1__7_segment_8,
       lcd_controller_1__7_segment_9;
  wire [31:0] mainfunc_1_t8;

  MainFunc mainfunc_1 (
    .Write__t9(to__t9), .Write_Signal(keypad_controller_1_write), .t8(mainfunc_1_t8), .t9(From__t9));  // open: Output_of_Address, Opcode, Read_Data_2, _9
  _7_Segment_Display u_7_segment_display_1 (
    .g(lcd_controller_1_minus[0]), .f(lcd_controller_1_minus[1]), .a(lcd_controller_1_minus[2]),
    .b(lcd_controller_1_minus[3]), .e(lcd_controller_1_minus_2[0]), .d(lcd_controller_1_minus_2[1]),
    .c(lcd_controller_1_minus_2[2]));  // open: dp
  _7_Segment_Display u_7_segment_display_2 (
    .g(lcd_controller_1__7_segment_9[0]), .f(lcd_controller_1__7_segment_9[1]),
    .a(lcd_controller_1__7_segment_9[2]), .b(lcd_controller_1__7_segment_9[3]),
    .e(lcd_controller_1__7_segment_9[4]), .d(lcd_controller_1__7_segment_9[5]),
    .c(lcd_controller_1__7_segment_9[6]));  // open: dp
  LCD_Controller lcd_controller_1 (
    .From__t8(mainfunc_1_t8), .Minus({lcd_controller_1_minus_2, lcd_controller_1_minus}),
    ._7_Segment_9(lcd_controller_1__7_segment_9), ._7_Segment_8(lcd_controller_1__7_segment_8),
    ._7_Segment_7({lcd_controller_1__7_segment_7_2, lcd_controller_1__7_segment_7}),
    ._7_Segment_6({lcd_controller_1__7_segment_6_2, lcd_controller_1__7_segment_6}),
    ._7_Segment_5(lcd_controller_1__7_segment_5),
    ._7_Segment_4({lcd_controller_1__7_segment_4_2, lcd_controller_1__7_segment_4}),
    ._7_Segment_3({lcd_controller_1__7_segment_3_2, lcd_controller_1__7_segment_3}),
    ._7_Segment_2({lcd_controller_1__7_segment_2_2, lcd_controller_1__7_segment_2}),
    ._7_Segment_1(lcd_controller_1__7_segment_1),
    ._7_Segment_0({lcd_controller_1__7_segment_0_2, lcd_controller_1__7_segment_0}));
  Keypad_Controller keypad_controller_1 (
    .C(C_out), .in_2(button_out), .in_3(button_5_out), .in_4(button_4_out), .in_5(button_3_out),
    .in_6(button_2_out), ._9(_9_out), ._8(_8_out), ._7(_7_out), ._6(_6_out), ._5(_5_out), ._4(_4_out),
    ._3(_3_out), ._2(_2_out), ._1(_1_out), ._0(_0_out), .From__t9(From__t9),
    .Write(keypad_controller_1_write), .Output(to__t9));
  _7_Segment_Display u_7_segment_display_3 (
    .g(lcd_controller_1__7_segment_7[0]), .f(lcd_controller_1__7_segment_7[1]),
    .a(lcd_controller_1__7_segment_7[2]), .b(lcd_controller_1__7_segment_7[3]),
    .e(lcd_controller_1__7_segment_7_2[0]), .d(lcd_controller_1__7_segment_7_2[1]),
    .c(lcd_controller_1__7_segment_7_2[2]));  // open: dp
  _7_Segment_Display u_7_segment_display_4 (
    .g(lcd_controller_1__7_segment_8[0]), .f(lcd_controller_1__7_segment_8[1]),
    .a(lcd_controller_1__7_segment_8[2]), .b(lcd_controller_1__7_segment_8[3]),
    .e(lcd_controller_1__7_segment_8[4]), .d(lcd_controller_1__7_segment_8[5]),
    .c(lcd_controller_1__7_segment_8[6]));  // open: dp
  _7_Segment_Display u_7_segment_display_5 (
    .g(lcd_controller_1__7_segment_6[0]), .f(lcd_controller_1__7_segment_6[1]),
    .a(lcd_controller_1__7_segment_6[2]), .b(lcd_controller_1__7_segment_6[3]),
    .e(lcd_controller_1__7_segment_6_2[0]), .d(lcd_controller_1__7_segment_6_2[1]),
    .c(lcd_controller_1__7_segment_6_2[2]));  // open: dp
  _7_Segment_Display u_7_segment_display_6 (
    .g(lcd_controller_1__7_segment_5[0]), .f(lcd_controller_1__7_segment_5[1]),
    .a(lcd_controller_1__7_segment_5[2]), .b(lcd_controller_1__7_segment_5[3]),
    .e(lcd_controller_1__7_segment_5[4]), .d(lcd_controller_1__7_segment_5[5]),
    .c(lcd_controller_1__7_segment_5[6]));  // open: dp
  Button _7 (.out(_7_out));
  Button _4 (.out(_4_out));
  Button _1 (.out(_1_out));
  Button _0 (.out(_0_out));
  _7_Segment_Display u_7_segment_display_7 (
    .g(lcd_controller_1__7_segment_4[0]), .f(lcd_controller_1__7_segment_4[1]),
    .a(lcd_controller_1__7_segment_4[2]), .b(lcd_controller_1__7_segment_4[3]),
    .e(lcd_controller_1__7_segment_4_2[0]), .d(lcd_controller_1__7_segment_4_2[1]),
    .c(lcd_controller_1__7_segment_4_2[2]));  // open: dp
  _7_Segment_Display u_7_segment_display_8 (
    .g(lcd_controller_1__7_segment_3[0]), .f(lcd_controller_1__7_segment_3[1]),
    .a(lcd_controller_1__7_segment_3[2]), .b(lcd_controller_1__7_segment_3[3]),
    .e(lcd_controller_1__7_segment_3_2[0]), .d(lcd_controller_1__7_segment_3_2[1]),
    .c(lcd_controller_1__7_segment_3_2[2]));  // open: dp
  Button _8 (.out(_8_out));
  Button _5 (.out(_5_out));
  Button _2 (.out(_2_out));
  Button C (.out(C_out));
  _7_Segment_Display u_7_segment_display_9 (
    .g(lcd_controller_1__7_segment_2[0]), .f(lcd_controller_1__7_segment_2[1]),
    .a(lcd_controller_1__7_segment_2[2]), .b(lcd_controller_1__7_segment_2[3]),
    .e(lcd_controller_1__7_segment_2_2[0]), .d(lcd_controller_1__7_segment_2_2[1]),
    .c(lcd_controller_1__7_segment_2_2[2]));  // open: dp
  _7_Segment_Display u_7_segment_display_10 (
    .g(lcd_controller_1__7_segment_1[0]), .f(lcd_controller_1__7_segment_1[1]),
    .a(lcd_controller_1__7_segment_1[2]), .b(lcd_controller_1__7_segment_1[3]),
    .e(lcd_controller_1__7_segment_1[4]), .d(lcd_controller_1__7_segment_1[5]),
    .c(lcd_controller_1__7_segment_1[6]));  // open: dp
  Button _9 (.out(_9_out));
  Button _6 (.out(_6_out));
  Button _3 (.out(_3_out));
  Button button (.out(button_out));
  _7_Segment_Display u_7_segment_display_11 (
    .g(lcd_controller_1__7_segment_0[0]), .f(lcd_controller_1__7_segment_0[1]),
    .a(lcd_controller_1__7_segment_0[2]), .b(lcd_controller_1__7_segment_0[3]),
    .e(lcd_controller_1__7_segment_0_2[0]), .d(lcd_controller_1__7_segment_0_2[1]),
    .c(lcd_controller_1__7_segment_0_2[2]));  // open: dp
  Button button_2 (.out(button_2_out));
  Button button_3 (.out(button_3_out));
  Button button_4 (.out(button_4_out));
  Button button_5 (.out(button_5_out));

  // Notes on the sheet:
  //   From $t8
  //   From $t9
  //   Write Data to $t9
  //   Write Signal for $t9
endmodule

module LCD_Controller (
  input  [31:0] From__t8,
  output [6:0] Minus,
  output [6:0] _7_Segment_9,
  output [6:0] _7_Segment_8,
  output [6:0] _7_Segment_7,
  output [6:0] _7_Segment_6,
  output [6:0] _7_Segment_5,
  output [6:0] _7_Segment_4,
  output [6:0] _7_Segment_3,
  output [6:0] _7_Segment_2,
  output [6:0] _7_Segment_1,
  output [6:0] _7_Segment_0
);

  wire [3:0] binarytobcd_1_bcd0, binarytobcd_1_bcd1, binarytobcd_1_bcd2, binarytobcd_1_bcd3,
       binarytobcd_1_bcd4, binarytobcd_1_bcd5, binarytobcd_1_bcd6, binarytobcd_1_bcd7, binarytobcd_1_bcd8,
       binarytobcd_1_bcd9;

  BinaryToBCD binarytobcd_1 (
    .Input(From__t8), .Minus(Minus[0]), .BCD9(binarytobcd_1_bcd9), .BCD8(binarytobcd_1_bcd8),
    .BCD7(binarytobcd_1_bcd7), .BCD6(binarytobcd_1_bcd6), .BCD5(binarytobcd_1_bcd5),
    .BCD4(binarytobcd_1_bcd4), .BCD3(binarytobcd_1_bcd3), .BCD2(binarytobcd_1_bcd2),
    .BCD1(binarytobcd_1_bcd1), .BCD0(binarytobcd_1_bcd0));
  _7_Segment_Controller u_7_segment_controller_1 (.BCD(binarytobcd_1_bcd9), .out_2(_7_Segment_9));
  _7_Segment_Controller u_7_segment_controller_2 (.BCD(binarytobcd_1_bcd8), .out_2(_7_Segment_8));
  _7_Segment_Controller u_7_segment_controller_3 (.BCD(binarytobcd_1_bcd7), .out_2(_7_Segment_7));
  _7_Segment_Controller u_7_segment_controller_4 (.BCD(binarytobcd_1_bcd6), .out_2(_7_Segment_6));
  _7_Segment_Controller u_7_segment_controller_5 (.BCD(binarytobcd_1_bcd5), .out_2(_7_Segment_5));
  _7_Segment_Controller u_7_segment_controller_6 (.BCD(binarytobcd_1_bcd4), .out_2(_7_Segment_4));
  _7_Segment_Controller u_7_segment_controller_7 (.BCD(binarytobcd_1_bcd3), .out_2(_7_Segment_3));
  _7_Segment_Controller u_7_segment_controller_8 (.BCD(binarytobcd_1_bcd2), .out_2(_7_Segment_2));
  _7_Segment_Controller u_7_segment_controller_9 (.BCD(binarytobcd_1_bcd1), .out_2(_7_Segment_1));
  _7_Segment_Controller u_7_segment_controller_10 (.BCD(binarytobcd_1_bcd0), .out_2(_7_Segment_0));

  assign Minus[6:1] = {6{1'b0}};
endmodule

module _7_Segment_Controller (
  input  [3:0] BCD,
  output [6:0] out_2
);

  wire and_1_out, and_2_out, and_3_out, and_4_out, and_5_out, and_6_out, and_7_out, and_8_out, and_9_out,
       and_10_out, and_11_out, and_12_out, and_13_out, and_14_out, and_15_out, and_16_out, not_1_out,
       not_2_out, not_3_out, not_4_out, not_5_out, not_6_out, not_7_out, not_8_out, not_9_out, not_10_out,
       not_11_out, not_12_out, not_13_out, not_14_out, not_15_out, not_16_out, not_17_out, not_18_out,
       not_19_out, not_20_out, not_21_out;

  not not_1 (not_1_out, BCD[2]);
  not not_2 (not_2_out, BCD[0]);
  not not_3 (not_3_out, BCD[1]);
  not not_4 (not_4_out, BCD[1]);
  not not_5 (not_5_out, BCD[0]);
  not not_6 (not_6_out, BCD[1]);
  not not_7 (not_7_out, BCD[0]);
  not not_8 (not_8_out, BCD[2]);
  not not_9 (not_9_out, BCD[0]);
  not not_10 (not_10_out, BCD[1]);
  not not_11 (not_11_out, BCD[0]);
  not not_12 (not_12_out, BCD[2]);
  not not_13 (not_13_out, BCD[0]);
  not not_14 (not_14_out, BCD[0]);
  not not_15 (not_15_out, BCD[2]);
  not not_16 (not_16_out, BCD[0]);
  not not_17 (not_17_out, BCD[2]);
  not not_18 (not_18_out, BCD[0]);
  not not_19 (not_19_out, BCD[1]);
  not not_20 (not_20_out, BCD[1]);
  and and_1 (and_1_out, not_1_out, BCD[1]);
  and and_2 (and_2_out, BCD[1], not_2_out);
  and and_3 (and_3_out, BCD[2], not_3_out);
  and and_4 (and_4_out, not_4_out, not_5_out);
  and and_5 (and_5_out, BCD[2], not_6_out);
  and and_6 (and_6_out, BCD[2], not_7_out);
  and and_7 (and_7_out, not_8_out, not_9_out);
  and and_8 (and_8_out, BCD[2], BCD[0]);
  not not_21 (not_21_out, BCD[2]);
  and and_9 (and_9_out, not_10_out, not_11_out);
  and and_10 (and_10_out, BCD[1], BCD[0]);
  and and_11 (and_11_out, not_12_out, not_13_out);
  and and_12 (and_12_out, BCD[1], not_14_out);
  and and_13 (and_13_out, not_15_out, not_16_out);
  and and_14 (and_14_out, not_17_out, BCD[1]);
  and and_15 (and_15_out, BCD[1], not_18_out);
  and and_16 (and_16_out, BCD[2], not_19_out, BCD[0]);
  or or_1 (out_2[6], not_20_out, BCD[0], BCD[2]);
  or or_2 (out_2[0], and_1_out, and_2_out, and_3_out, BCD[3]);
  or or_3 (out_2[1], and_4_out, and_5_out, and_6_out, BCD[3]);
  or or_4 (out_2[2], and_7_out, BCD[1], and_8_out, BCD[3]);
  or or_5 (out_2[3], not_21_out, and_9_out, and_10_out);
  or or_6 (out_2[4], and_11_out, and_12_out);
  or or_7 (out_2[5], and_13_out, and_14_out, and_15_out, and_16_out);
endmodule

module BinaryToBCD (
  input  [31:0] Input,
  output Minus,
  output [3:0] BCD9,
  output [3:0] BCD8,
  output [3:0] BCD7,
  output [3:0] BCD6,
  output [3:0] BCD5,
  output [3:0] BCD4,
  output [3:0] BCD3,
  output [3:0] BCD2,
  output [3:0] BCD1,
  output [3:0] BCD0
);

  wire [27:0] subtractor_1_out, subtractor_2_out, subtractor_3_out, subtractor_4_out, subtractor_5_out,
       subtractor_6_out, subtractor_7_out, subtractor_8_out, subtractor_9_out;
  wire [31:0] adder_1_out, divider_1_out, divider_2_out, divider_3_out, divider_4_out, divider_5_out,
       divider_6_out, divider_7_out, divider_8_out, multiplexer_1_out, multiplier_1_out, multiplier_2_out,
       multiplier_3_out, multiplier_4_out, multiplier_5_out, multiplier_6_out, multiplier_7_out,
       multiplier_8_out, multiplier_9_out, not_1_out;
  wire [31:4] divider_9_out;

  assign not_1_out = ~Input;  // NOT_Gate not_1, 32 bits wide
  Adder #(.width(32)) adder_1 (.a(not_1_out), .b(32'h1), .out(adder_1_out));  // open: cin, cout
  Multiplexer #(.width(32)) multiplexer_1 (
    .in0(Input), .in1(adder_1_out), .out(multiplexer_1_out), .sel(Input[31]));  // open: en
  Subtractor #(.width(32)) subtractor_1 (
    .a(multiplexer_1_out), .b(multiplier_1_out), .out({subtractor_1_out, BCD0}));  // open: bin, bout
  Multiplier #(.width(32)) multiplier_1 (.a(divider_1_out), .b(32'ha), .out(multiplier_1_out));  // open: cin, cout
  Divider #(.width(32)) divider_1 (.a(multiplexer_1_out), .b(32'ha), .out(divider_1_out));  // open: upper, rem
  Subtractor #(.width(32)) subtractor_2 (
    .a(divider_1_out), .b(multiplier_2_out), .out({subtractor_2_out, BCD1}));  // open: bin, bout
  Multiplier #(.width(32)) multiplier_2 (.a(divider_2_out), .b(32'ha), .out(multiplier_2_out));  // open: cin, cout
  Divider #(.width(32)) divider_2 (.a(divider_1_out), .b(32'ha), .out(divider_2_out));  // open: upper, rem
  Subtractor #(.width(32)) subtractor_3 (
    .a(divider_2_out), .b(multiplier_3_out), .out({subtractor_3_out, BCD2}));  // open: bin, bout
  Multiplier #(.width(32)) multiplier_3 (.a(divider_3_out), .b(32'ha), .out(multiplier_3_out));  // open: cin, cout
  Divider #(.width(32)) divider_3 (.a(divider_2_out), .b(32'ha), .out(divider_3_out));  // open: upper, rem
  Subtractor #(.width(32)) subtractor_4 (
    .a(divider_3_out), .b(multiplier_4_out), .out({subtractor_4_out, BCD3}));  // open: bin, bout
  Multiplier #(.width(32)) multiplier_4 (.a(divider_4_out), .b(32'ha), .out(multiplier_4_out));  // open: cin, cout
  Divider #(.width(32)) divider_4 (.a(divider_3_out), .b(32'ha), .out(divider_4_out));  // open: upper, rem
  Subtractor #(.width(32)) subtractor_5 (
    .a(divider_4_out), .b(multiplier_5_out), .out({subtractor_5_out, BCD4}));  // open: bin, bout
  Multiplier #(.width(32)) multiplier_5 (.a(divider_5_out), .b(32'ha), .out(multiplier_5_out));  // open: cin, cout
  Divider #(.width(32)) divider_5 (.a(divider_4_out), .b(32'ha), .out(divider_5_out));  // open: upper, rem
  Subtractor #(.width(32)) subtractor_6 (
    .a(divider_5_out), .b(multiplier_6_out), .out({subtractor_6_out, BCD5}));  // open: bin, bout
  Multiplier #(.width(32)) multiplier_6 (.a(divider_6_out), .b(32'ha), .out(multiplier_6_out));  // open: cin, cout
  Divider #(.width(32)) divider_6 (.a(divider_5_out), .b(32'ha), .out(divider_6_out));  // open: upper, rem
  Subtractor #(.width(32)) subtractor_7 (
    .a(divider_6_out), .b(multiplier_7_out), .out({subtractor_7_out, BCD6}));  // open: bin, bout
  Multiplier #(.width(32)) multiplier_7 (.a(divider_7_out), .b(32'ha), .out(multiplier_7_out));  // open: cin, cout
  Divider #(.width(32)) divider_7 (.a(divider_6_out), .b(32'ha), .out(divider_7_out));  // open: upper, rem
  Subtractor #(.width(32)) subtractor_8 (
    .a(divider_7_out), .b(multiplier_8_out), .out({subtractor_8_out, BCD7}));  // open: bin, bout
  Multiplier #(.width(32)) multiplier_8 (.a(divider_8_out), .b(32'ha), .out(multiplier_8_out));  // open: cin, cout
  Divider #(.width(32)) divider_8 (.a(divider_7_out), .b(32'ha), .out(divider_8_out));  // open: upper, rem
  Subtractor #(.width(32)) subtractor_9 (
    .a(divider_8_out), .b(multiplier_9_out), .out({subtractor_9_out, BCD8}));  // open: bin, bout
  Multiplier #(.width(32)) multiplier_9 (
    .a({divider_9_out, BCD9}), .b(32'ha), .out(multiplier_9_out));  // open: cin, cout
  Divider #(.width(32)) divider_9 (.a(divider_8_out), .b(32'ha), .out({divider_9_out, BCD9}));  // open: upper, rem

  assign Minus = Input[31];
endmodule

module Keypad_Controller (
  input  C,
  input  in_2,
  input  in_3,
  input  in_4,
  input  in_5,
  input  in_6,
  input  _9,
  input  _8,
  input  _7,
  input  _6,
  input  _5,
  input  _4,
  input  _3,
  input  _2,
  input  _1,
  input  _0,
  input  [31:0] From__t9,
  output Write,
  output [31:0] Output
);

  wire iszero_1_out_2, iszero_2_out_2;
  wire [3:0] or_4_out;
  wire [15:0] and_1_out;

  and and_1 (and_1_out[0], C, iszero_1_out_2);
  and and_2 (and_1_out[1], in_2, iszero_1_out_2);
  and and_3 (and_1_out[2], in_3, iszero_1_out_2);
  and and_4 (and_1_out[3], in_4, iszero_1_out_2);
  and and_5 (and_1_out[4], in_5, iszero_1_out_2);
  and and_6 (and_1_out[5], in_6, iszero_1_out_2);
  and and_7 (and_1_out[6], _9, iszero_1_out_2);
  and and_8 (and_1_out[7], _8, iszero_1_out_2);
  and and_9 (and_1_out[8], _7, iszero_1_out_2);
  and and_10 (and_1_out[9], _6, iszero_1_out_2);
  and and_11 (and_1_out[10], _5, iszero_1_out_2);
  and and_12 (and_1_out[11], _4, iszero_1_out_2);
  and and_13 (and_1_out[12], _3, iszero_1_out_2);
  and and_14 (and_1_out[13], _2, iszero_1_out_2);
  and and_15 (and_1_out[14], _1, iszero_1_out_2);
  and and_16 (and_1_out[15], _0, iszero_1_out_2);
  isZero iszero_1 (.Input(From__t9), .out_2(iszero_1_out_2));
  or or_1 (or_4_out[3], and_1_out[0], and_1_out[1], and_1_out[2], and_1_out[3], and_1_out[4], and_1_out[5], and_1_out[6], and_1_out[7]);
  or or_2 (or_4_out[2], and_1_out[8], and_1_out[9], and_1_out[10], and_1_out[11], and_1_out[0], and_1_out[1], and_1_out[2], and_1_out[3]);
  or or_3 (or_4_out[1], and_1_out[12], and_1_out[13], and_1_out[9], and_1_out[8], and_1_out[5], and_1_out[4], and_1_out[1], and_1_out[0]);
  or or_4 (or_4_out[0], and_1_out[12], and_1_out[14], and_1_out[10], and_1_out[8], and_1_out[6], and_1_out[4], and_1_out[2], and_1_out[0]);
  isZero iszero_2 (.Input({{16{1'b0}}, and_1_out}), .out_2(iszero_2_out_2));
  not not_1 (Write, iszero_2_out_2);
  assign Output = Write ? {28'h8000000, or_4_out} : 32'bz;  // Controlled_Buffer controlled_buffer_1
endmodule

module isZero (
  input  [31:0] Input,
  output out_2
);

  wire or_1_out;

  not not_1 (out_2, or_1_out);
  or or_1 (or_1_out, Input[0], Input[1], Input[2], Input[3], Input[4], Input[5], Input[6], Input[7], Input[8], Input[9], Input[10], Input[11], Input[12], Input[13], Input[14], Input[15], Input[16], Input[17], Input[18], Input[19], Input[20], Input[21], Input[22], Input[23], Input[24], Input[25], Input[26], Input[27], Input[28], Input[29], Input[30], Input[31]);
endmodule

module Instruction_Memory__TO_DO (
  input  [15:0] Input,
  output [31:0] out_2
);

  ROM #(.addrWidth(16), .dataWidth(32)) rom_1 (.addr(Input), .data(out_2));  // open: sel

  // Notes on the sheet:
  //   contents of rom_1 (hex, n*v repeats v):
  //   20180000 c820 8100003 1320ffff 20100000 3204020 84040 84042 2001000a 10280031 2001000b 10280035
  //   2001000c 1028003b 2001000d 1028003f 2001000e 10280043 2001000f 1028006c 21310000 810001a 20160001
  //   20080000 20190000 8100003 20010009 1430000b 21310000 1284820 120c020 20010001 10360002 c820 8100036
  //   c820 15600014 18c022 8100036 1314820 22100001 2001000a 10280010 2001000b 10280014 2001000c 1028001a
  //   2001000d 1028001e 2001000e 10280022 2001000f 1028004b 810001a 15600002 230a0000 8100003 230c0000
  //   8100003 210b0000 20080000 20090000 20190000 20180000 8100003 20010000 102affd3 210b0000 20080000
  //   20090000 20190000 20180000 8100003 210b0000 20080000 20090000 20190000 20180000 8100003 210b0000
  //   20080000 20090000 20190000 20180000 8100003 2001000a 102b0006 2001000b 102b0008 2001000c 102b000a
  //   2001000d 102b0010 18a6820 1a0c020 20080000 8100090 14c6822 1a0c020 20080000 8100090 158e0004 1a0c020
  //   20080000 200c0000 8100090 14d6820 21ce0001 8100065 140a82a 20010001 10350008 14c982a 1260000b
  //   20010001 10340007 1a0c020 20080000 200c0000 8100090 a5022 20140001 8100070 d6822 8100074 14c5022
  //   21ad0001 810006d 200b0000 20080000 20090000 200a0000 200c0000 200d0000 20100000 20110000 20120000
  //   20130000 20190000 20180000 200e0000 20140000 20150000 8100000 210b0000 20080000 20090000 200a0000
  //   200c0000 200d0000 200e0000 20100000 20110000 20120000 20130000 20140000 20160000 20190000 810009f
  //   1320ffff 20100000 230a0000 3204020 84040 84042 2001000a 1028ff94 2001000b 1028ff98 2001000c 1028ff9e
  //   2001000d 1028ffa2 2001000e 1028ffa6 2001000f 1028ffcf 21310000 810001a
endmodule

module Shift_Left__TO_DO (
  input  [31:0] Input,
  input  [4:0] Shifter,
  output [31:0] Result
);

  Shifter #(.width(32)) shifter_1 (.in(Input), .\dist (Shifter), .out(Result));
endmodule

module Shift_Right__TO_DO (
  input  [31:0] Input,
  input  [4:0] Shifter,
  output [31:0] Result
);

  Shifter #(.width(32), .shift("lr")) shifter_1 (.in(Input), .\dist (Shifter), .out(Result));
endmodule

module Sign_Extend__TO_DO (
  input  [15:0] Input,
  output [31:0] Extended_Bit
);


  assign Extended_Bit = {{17{Input[15]}}, Input[14:0]};
endmodule

module _32_bit_ALU__TO_DO (
  input  [3:0] ALU_Operation,
  input  [31:0] B,
  input  [31:0] A,
  output Zero,
  output [31:0] Main_Result,
  output OverFlow
);

  wire _0_carry_out, _1_carry_out, _2_carry_out, _3_carry_out, _4_carry_out, _5_carry_out, _6_carry_out,
       _7_carry_out, _8_carry_out, _9_carry_out, _10_carry_out, _11_carry_out, _12_carry_out, _13_carry_out,
       _14_carry_out, _15_carry_out, _16_carry_out, _18_carry_out, _19_carry_out, _20_carry_out,
       _21_carry_out, _22_carry_out, _23_carry_out, _24_carry_out, _25_carry_out, _26_carry_out,
       _27_carry_out, _28_carry_out, _29_carry_out, _30_carry_out, _31_set, n1_bit_alu_1_carry_out, or_1_out;

  _1_Bit_ALU _0 (
    .A(B[0]), .B(A[0]), .Less(_31_set), .Carry_In(ALU_Operation[2]), .AInvert(ALU_Operation[2]),
    .BInvert(ALU_Operation[3]), .Carry_Out(_0_carry_out), .Operation(ALU_Operation[1:0]),
    .Result(Main_Result[0]));  // open: Set
  _1_Bit_ALU _1 (
    .A(B[1]), .B(A[1]), .Less(1'b0), .Carry_In(_0_carry_out), .AInvert(ALU_Operation[2]),
    .BInvert(ALU_Operation[3]), .Carry_Out(_1_carry_out), .Operation(ALU_Operation[1:0]),
    .Result(Main_Result[1]));  // open: Set
  _1_Bit_ALU _2 (
    .A(B[2]), .B(A[2]), .Less(1'b0), .Carry_In(_1_carry_out), .AInvert(ALU_Operation[2]),
    .BInvert(ALU_Operation[3]), .Carry_Out(_2_carry_out), .Operation(ALU_Operation[1:0]),
    .Result(Main_Result[2]));  // open: Set
  _1_Bit_ALU _3 (
    .A(B[3]), .B(A[3]), .Less(1'b0), .Carry_In(_2_carry_out), .AInvert(ALU_Operation[2]),
    .BInvert(ALU_Operation[3]), .Carry_Out(_3_carry_out), .Operation(ALU_Operation[1:0]),
    .Result(Main_Result[3]));  // open: Set
  _1_Bit_ALU _4 (
    .A(B[4]), .B(A[4]), .Less(1'b0), .Carry_In(_3_carry_out), .AInvert(ALU_Operation[2]),
    .BInvert(ALU_Operation[3]), .Carry_Out(_4_carry_out), .Operation(ALU_Operation[1:0]),
    .Result(Main_Result[4]));  // open: Set
  _1_Bit_ALU _5 (
    .A(B[5]), .B(A[5]), .Less(1'b0), .Carry_In(_4_carry_out), .AInvert(ALU_Operation[2]),
    .BInvert(ALU_Operation[3]), .Carry_Out(_5_carry_out), .Operation(ALU_Operation[1:0]),
    .Result(Main_Result[5]));  // open: Set
  _1_Bit_ALU _6 (
    .A(B[6]), .B(A[6]), .Less(1'b0), .Carry_In(_5_carry_out), .AInvert(ALU_Operation[2]),
    .BInvert(ALU_Operation[3]), .Carry_Out(_6_carry_out), .Operation(ALU_Operation[1:0]),
    .Result(Main_Result[6]));  // open: Set
  _1_Bit_ALU _7 (
    .A(B[7]), .B(A[7]), .Less(1'b0), .Carry_In(_6_carry_out), .AInvert(ALU_Operation[2]),
    .BInvert(ALU_Operation[3]), .Carry_Out(_7_carry_out), .Operation(ALU_Operation[1:0]),
    .Result(Main_Result[7]));  // open: Set
  _1_Bit_ALU _8 (
    .A(B[8]), .B(A[8]), .Less(1'b0), .Carry_In(_7_carry_out), .AInvert(ALU_Operation[2]),
    .BInvert(ALU_Operation[3]), .Carry_Out(_8_carry_out), .Operation(ALU_Operation[1:0]),
    .Result(Main_Result[8]));  // open: Set
  _1_Bit_ALU _9 (
    .A(B[9]), .B(A[9]), .Less(1'b0), .Carry_In(_8_carry_out), .AInvert(ALU_Operation[2]),
    .BInvert(ALU_Operation[3]), .Carry_Out(_9_carry_out), .Operation(ALU_Operation[1:0]),
    .Result(Main_Result[9]));  // open: Set
  _1_Bit_ALU _10 (
    .A(B[10]), .B(A[10]), .Less(1'b0), .Carry_In(_9_carry_out), .AInvert(ALU_Operation[2]),
    .BInvert(ALU_Operation[3]), .Carry_Out(_10_carry_out), .Operation(ALU_Operation[1:0]),
    .Result(Main_Result[10]));  // open: Set
  _1_Bit_ALU _11 (
    .A(B[11]), .B(A[11]), .Less(1'b0), .Carry_In(_10_carry_out), .AInvert(ALU_Operation[2]),
    .BInvert(ALU_Operation[3]), .Carry_Out(_11_carry_out), .Operation(ALU_Operation[1:0]),
    .Result(Main_Result[11]));  // open: Set
  _1_Bit_ALU _12 (
    .A(B[12]), .B(A[12]), .Less(1'b0), .Carry_In(_11_carry_out), .AInvert(ALU_Operation[2]),
    .BInvert(ALU_Operation[3]), .Carry_Out(_12_carry_out), .Operation(ALU_Operation[1:0]),
    .Result(Main_Result[12]));  // open: Set
  _1_Bit_ALU _13 (
    .A(B[13]), .B(A[13]), .Less(1'b0), .Carry_In(_12_carry_out), .AInvert(ALU_Operation[2]),
    .BInvert(ALU_Operation[3]), .Carry_Out(_13_carry_out), .Operation(ALU_Operation[1:0]),
    .Result(Main_Result[13]));  // open: Set
  _1_Bit_ALU _14 (
    .A(B[14]), .B(A[14]), .Less(1'b0), .Carry_In(_13_carry_out), .AInvert(ALU_Operation[2]),
    .BInvert(ALU_Operation[3]), .Carry_Out(_14_carry_out), .Operation(ALU_Operation[1:0]),
    .Result(Main_Result[14]));  // open: Set
  _1_Bit_ALU _15 (
    .A(B[15]), .B(A[15]), .Less(1'b0), .Carry_In(_14_carry_out), .AInvert(ALU_Operation[2]),
    .BInvert(ALU_Operation[3]), .Carry_Out(_15_carry_out), .Operation(ALU_Operation[1:0]),
    .Result(Main_Result[15]));  // open: Set
  _1_Bit_ALU _16 (
    .A(B[16]), .B(A[16]), .Less(1'b0), .Carry_In(_15_carry_out), .AInvert(ALU_Operation[2]),
    .BInvert(ALU_Operation[3]), .Carry_Out(_16_carry_out), .Operation(ALU_Operation[1:0]),
    .Result(Main_Result[16]));  // open: Set
  _1_Bit_ALU u_1_bit_alu_1 (
    .A(B[17]), .B(A[17]), .Less(1'b0), .Carry_In(_16_carry_out), .AInvert(ALU_Operation[2]),
    .BInvert(ALU_Operation[3]), .Carry_Out(n1_bit_alu_1_carry_out), .Operation(ALU_Operation[1:0]),
    .Result(Main_Result[17]));  // open: Set
  _1_Bit_ALU _18 (
    .A(B[18]), .B(A[18]), .Less(1'b0), .Carry_In(n1_bit_alu_1_carry_out), .AInvert(ALU_Operation[2]),
    .BInvert(ALU_Operation[3]), .Carry_Out(_18_carry_out), .Operation(ALU_Operation[1:0]),
    .Result(Main_Result[18]));  // open: Set
  _1_Bit_ALU _19 (
    .A(B[19]), .B(A[19]), .Less(1'b0), .Carry_In(_18_carry_out), .AInvert(ALU_Operation[2]),
    .BInvert(ALU_Operation[3]), .Carry_Out(_19_carry_out), .Operation(ALU_Operation[1:0]),
    .Result(Main_Result[19]));  // open: Set
  _1_Bit_ALU _20 (
    .A(B[20]), .B(A[20]), .Less(1'b0), .Carry_In(_19_carry_out), .AInvert(ALU_Operation[2]),
    .BInvert(ALU_Operation[3]), .Carry_Out(_20_carry_out), .Operation(ALU_Operation[1:0]),
    .Result(Main_Result[20]));  // open: Set
  _1_Bit_ALU _21 (
    .A(B[21]), .B(A[21]), .Less(1'b0), .Carry_In(_20_carry_out), .AInvert(ALU_Operation[2]),
    .BInvert(ALU_Operation[3]), .Carry_Out(_21_carry_out), .Operation(ALU_Operation[1:0]),
    .Result(Main_Result[21]));  // open: Set
  _1_Bit_ALU _22 (
    .A(B[22]), .B(A[22]), .Less(1'b0), .Carry_In(_21_carry_out), .AInvert(ALU_Operation[2]),
    .BInvert(ALU_Operation[3]), .Carry_Out(_22_carry_out), .Operation(ALU_Operation[1:0]),
    .Result(Main_Result[22]));  // open: Set
  _1_Bit_ALU _23 (
    .A(B[23]), .B(A[23]), .Less(1'b0), .Carry_In(_22_carry_out), .AInvert(ALU_Operation[2]),
    .BInvert(ALU_Operation[3]), .Carry_Out(_23_carry_out), .Operation(ALU_Operation[1:0]),
    .Result(Main_Result[23]));  // open: Set
  _1_Bit_ALU _24 (
    .A(B[24]), .B(A[24]), .Less(1'b0), .Carry_In(_23_carry_out), .AInvert(ALU_Operation[2]),
    .BInvert(ALU_Operation[3]), .Carry_Out(_24_carry_out), .Operation(ALU_Operation[1:0]),
    .Result(Main_Result[24]));  // open: Set
  _1_Bit_ALU _25 (
    .A(B[25]), .B(A[25]), .Less(1'b0), .Carry_In(_24_carry_out), .AInvert(ALU_Operation[2]),
    .BInvert(ALU_Operation[3]), .Carry_Out(_25_carry_out), .Operation(ALU_Operation[1:0]),
    .Result(Main_Result[25]));  // open: Set
  _1_Bit_ALU _26 (
    .A(B[26]), .B(A[26]), .Less(1'b0), .Carry_In(_25_carry_out), .AInvert(ALU_Operation[2]),
    .BInvert(ALU_Operation[3]), .Carry_Out(_26_carry_out), .Operation(ALU_Operation[1:0]),
    .Result(Main_Result[26]));  // open: Set
  _1_Bit_ALU _27 (
    .A(B[27]), .B(A[27]), .Less(1'b0), .Carry_In(_26_carry_out), .AInvert(ALU_Operation[2]),
    .BInvert(ALU_Operation[3]), .Carry_Out(_27_carry_out), .Operation(ALU_Operation[1:0]),
    .Result(Main_Result[27]));  // open: Set
  _1_Bit_ALU _28 (
    .A(B[28]), .B(A[28]), .Less(1'b0), .Carry_In(_27_carry_out), .AInvert(ALU_Operation[2]),
    .BInvert(ALU_Operation[3]), .Carry_Out(_28_carry_out), .Operation(ALU_Operation[1:0]),
    .Result(Main_Result[28]));  // open: Set
  _1_Bit_ALU _29 (
    .A(B[29]), .B(A[29]), .Less(1'b0), .Carry_In(_28_carry_out), .AInvert(ALU_Operation[2]),
    .BInvert(ALU_Operation[3]), .Carry_Out(_29_carry_out), .Operation(ALU_Operation[1:0]),
    .Result(Main_Result[29]));  // open: Set
  _1_Bit_ALU _30 (
    .A(B[30]), .B(A[30]), .Less(1'b0), .Carry_In(_29_carry_out), .AInvert(ALU_Operation[2]),
    .BInvert(ALU_Operation[3]), .Carry_Out(_30_carry_out), .Operation(ALU_Operation[1:0]),
    .Result(Main_Result[30]));  // open: Set
  _1_Bit_ALU _31 (
    .A(B[31]), .B(A[31]), .Less(1'b0), .Carry_In(_30_carry_out), .AInvert(ALU_Operation[2]),
    .BInvert(ALU_Operation[3]), .Carry_Out(OverFlow), .Operation(ALU_Operation[1:0]),
    .Result(Main_Result[31]), .Set(_31_set));
  or or_1 (or_1_out, Main_Result[0], Main_Result[1], Main_Result[2], Main_Result[3], Main_Result[4], Main_Result[5], Main_Result[6], Main_Result[7], Main_Result[8], Main_Result[9], Main_Result[10], Main_Result[11], Main_Result[12], Main_Result[13], Main_Result[14], Main_Result[15], Main_Result[16], Main_Result[17], Main_Result[18], Main_Result[19], Main_Result[20], Main_Result[21], Main_Result[22], Main_Result[23], Main_Result[24], Main_Result[25], Main_Result[26], Main_Result[27], Main_Result[28], Main_Result[29], Main_Result[30], Main_Result[31]);
  not not_1 (Zero, or_1_out);
endmodule

module Register_File__TO_DO (
  input  RegWrite,
  input  [4:0] Read_Register1,
  input  [4:0] Read_Register_2,
  input  [4:0] Write_Register,
  input  [31:0] Write_Data,
  input  [31:0] Write_to__t9,
  input  Write_Signal,
  output [31:0] Read_Data_1,
  output [31:0] Read_Data_2,
  output [31:0] _9,
  output [31:0] t8,
  output [31:0] t9
);

  wire and_1_out, and_2_out, and_3_out, and_4_out, and_5_out, and_6_out, and_7_out, and_8_out, and_9_out,
       and_10_out, and_11_out, and_12_out, and_13_out, and_14_out, and_15_out, and_16_out, and_17_out,
       and_18_out, and_19_out, and_20_out, and_21_out, and_22_out, and_23_out, and_24_out, and_25_out,
       and_26_out, and_27_out, and_28_out, and_29_out, and_30_out, and_31_out, and_32_out, clock_1_out,
       controlled_buffer_3_out, decoder_1_out0, decoder_1_out1, decoder_1_out2, decoder_1_out3,
       decoder_1_out4, decoder_1_out5, decoder_1_out6, decoder_1_out7, decoder_1_out8, decoder_1_out9,
       decoder_1_out10, decoder_1_out11, decoder_1_out12, decoder_1_out13, decoder_1_out14, decoder_1_out15,
       decoder_1_out16, decoder_1_out17, decoder_1_out18, decoder_1_out19, decoder_1_out20, decoder_1_out21,
       decoder_1_out22, decoder_1_out23, decoder_1_out24, decoder_1_out25, decoder_1_out26, decoder_1_out27,
       decoder_1_out28, decoder_1_out29, decoder_1_out30, decoder_1_out31;
  wire [31:0] _0_q, _1_q, _2_q, _3_q, _4_q, _5_q, _6_q, _7_q, _8_q, _10_q, _11_q, _12_q, _13_q, _14_q, _15_q,
       _16_q, _17_q, _18_q, _19_q, _20_q, _21_q, _22_q, _23_q, _26_q, _27_q, _28_q, _29_q, _30_q, _31_q,
       controlled_buffer_1_out;

  Decoder #(.select(5)) decoder_1 (
    .out0(decoder_1_out0), .out1(decoder_1_out1), .out2(decoder_1_out2), .out3(decoder_1_out3),
    .out4(decoder_1_out4), .out5(decoder_1_out5), .out6(decoder_1_out6), .out7(decoder_1_out7),
    .out8(decoder_1_out8), .out9(decoder_1_out9), .out10(decoder_1_out10), .out11(decoder_1_out11),
    .out12(decoder_1_out12), .out13(decoder_1_out13), .out14(decoder_1_out14), .out15(decoder_1_out15),
    .out16(decoder_1_out16), .out17(decoder_1_out17), .out18(decoder_1_out18), .out19(decoder_1_out19),
    .out20(decoder_1_out20), .out21(decoder_1_out21), .out22(decoder_1_out22), .out23(decoder_1_out23),
    .out24(decoder_1_out24), .out25(decoder_1_out25), .out26(decoder_1_out26), .out27(decoder_1_out27),
    .out28(decoder_1_out28), .out29(decoder_1_out29), .out30(decoder_1_out30), .out31(decoder_1_out31),
    .sel(Write_Register));  // open: en
  assign controlled_buffer_1_out = Write_Signal ? Write_to__t9 : 32'bz;  // Controlled_Buffer controlled_buffer_1
  assign controlled_buffer_1_out = and_1_out ? Write_Data : 32'bz;  // Controlled_Buffer controlled_buffer_2
  assign controlled_buffer_3_out = and_1_out ? and_1_out : 1'bz;  // Controlled_Buffer controlled_buffer_3
  assign controlled_buffer_3_out = Write_Signal ? Write_Signal : 1'bz;  // Controlled_Buffer controlled_buffer_4
  and and_1 (and_1_out, decoder_1_out25, RegWrite);
  and and_2 (and_2_out, RegWrite, decoder_1_out0);
  and and_3 (and_3_out, decoder_1_out1, RegWrite);
  and and_4 (and_4_out, decoder_1_out2, RegWrite);
  and and_5 (and_5_out, decoder_1_out3, RegWrite);
  and and_6 (and_6_out, decoder_1_out4, RegWrite);
  and and_7 (and_7_out, decoder_1_out5, RegWrite);
  and and_8 (and_8_out, decoder_1_out6, RegWrite);
  and and_9 (and_9_out, decoder_1_out7, RegWrite);
  and and_10 (and_10_out, decoder_1_out8, RegWrite);
  and and_11 (and_11_out, RegWrite, decoder_1_out9);
  and and_12 (and_12_out, RegWrite, decoder_1_out10);
  and and_13 (and_13_out, RegWrite, decoder_1_out11);
  and and_14 (and_14_out, decoder_1_out12, RegWrite);
  and and_15 (and_15_out, RegWrite, decoder_1_out13);
  and and_16 (and_16_out, decoder_1_out14, RegWrite);
  and and_17 (and_17_out, decoder_1_out15, RegWrite);
  and and_18 (and_18_out, decoder_1_out16, RegWrite);
  and and_19 (and_19_out, decoder_1_out17, RegWrite);
  and and_20 (and_20_out, decoder_1_out18, RegWrite);
  and and_21 (and_21_out, decoder_1_out19, RegWrite);
  and and_22 (and_22_out, decoder_1_out20, RegWrite);
  and and_23 (and_23_out, decoder_1_out21, RegWrite);
  and and_24 (and_24_out, decoder_1_out22, RegWrite);
  and and_25 (and_25_out, decoder_1_out23, RegWrite);
  and and_26 (and_26_out, decoder_1_out24, RegWrite);
  and and_27 (and_27_out, decoder_1_out26, RegWrite);
  and and_28 (and_28_out, decoder_1_out27, RegWrite);
  and and_29 (and_29_out, decoder_1_out28, RegWrite);
  and and_30 (and_30_out, decoder_1_out29, RegWrite);
  and and_31 (and_31_out, decoder_1_out30, RegWrite);
  and and_32 (and_32_out, decoder_1_out31, RegWrite);
  Clock clock_1 (.out(clock_1_out));
  Register #(.width(32)) _0 (.D(Write_Data), .en(and_2_out), .Q(_0_q), .clk(clock_1_out));  // open: clr
  Register #(.width(32)) _1 (.D(Write_Data), .en(and_3_out), .Q(_1_q), .clk(clock_1_out));  // open: clr
  Register #(.width(32)) _2 (.D(Write_Data), .en(and_4_out), .Q(_2_q), .clk(clock_1_out));  // open: clr
  Register #(.width(32)) _3 (.D(Write_Data), .en(and_5_out), .Q(_3_q), .clk(clock_1_out));  // open: clr
  Register #(.width(32)) _4 (.D(Write_Data), .en(and_6_out), .Q(_4_q), .clk(clock_1_out));  // open: clr
  Register #(.width(32)) _5 (.D(Write_Data), .en(and_7_out), .Q(_5_q), .clk(clock_1_out));  // open: clr
  Register #(.width(32)) _6 (.D(Write_Data), .en(and_8_out), .Q(_6_q), .clk(clock_1_out));  // open: clr
  Register #(.width(32)) _7 (.D(Write_Data), .en(and_9_out), .Q(_7_q), .clk(clock_1_out));  // open: clr
  Register #(.width(32)) _8 (.D(Write_Data), .en(and_10_out), .Q(_8_q), .clk(clock_1_out));  // open: clr
  Register #(.width(32)) u__9 (.D(Write_Data), .en(and_11_out), .Q(_9), .clk(clock_1_out));  // open: clr
  Register #(.width(32)) _10 (.D(Write_Data), .en(and_12_out), .Q(_10_q), .clk(clock_1_out));  // open: clr
  Register #(.width(32)) _11 (.D(Write_Data), .en(and_13_out), .Q(_11_q), .clk(clock_1_out));  // open: clr
  Register #(.width(32)) _12 (.D(Write_Data), .en(and_14_out), .Q(_12_q), .clk(clock_1_out));  // open: clr
  Register #(.width(32)) _13 (.D(Write_Data), .en(and_15_out), .Q(_13_q), .clk(clock_1_out));  // open: clr
  Register #(.width(32)) _14 (.D(Write_Data), .en(and_16_out), .Q(_14_q), .clk(clock_1_out));  // open: clr
  Register #(.width(32)) _15 (.D(Write_Data), .en(and_17_out), .Q(_15_q), .clk(clock_1_out));  // open: clr
  Register #(.width(32)) _16 (.D(Write_Data), .en(and_18_out), .Q(_16_q), .clk(clock_1_out));  // open: clr
  Register #(.width(32)) _17 (.D(Write_Data), .en(and_19_out), .Q(_17_q), .clk(clock_1_out));  // open: clr
  Register #(.width(32)) _18 (.D(Write_Data), .en(and_20_out), .Q(_18_q), .clk(clock_1_out));  // open: clr
  Register #(.width(32)) _19 (.D(Write_Data), .en(and_21_out), .Q(_19_q), .clk(clock_1_out));  // open: clr
  Register #(.width(32)) _20 (.D(Write_Data), .en(and_22_out), .Q(_20_q), .clk(clock_1_out));  // open: clr
  Register #(.width(32)) _21 (.D(Write_Data), .en(and_23_out), .Q(_21_q), .clk(clock_1_out));  // open: clr
  Register #(.width(32)) _22 (.D(Write_Data), .en(and_24_out), .Q(_22_q), .clk(clock_1_out));  // open: clr
  Register #(.width(32)) _23 (.D(Write_Data), .en(and_25_out), .Q(_23_q), .clk(clock_1_out));  // open: clr
  Register #(.width(32)) _24 (.D(Write_Data), .en(and_26_out), .Q(t8), .clk(clock_1_out));  // open: clr
  Register #(.width(32)) _25 (
    .D(controlled_buffer_1_out), .en(controlled_buffer_3_out), .Q(t9), .clk(clock_1_out));  // open: clr
  Register #(.width(32)) _26 (.D(Write_Data), .en(and_27_out), .Q(_26_q), .clk(clock_1_out));  // open: clr
  Register #(.width(32)) _27 (.D(Write_Data), .en(and_28_out), .Q(_27_q), .clk(clock_1_out));  // open: clr
  Register #(.width(32)) _28 (.D(Write_Data), .en(and_29_out), .Q(_28_q), .clk(clock_1_out));  // open: clr
  Register #(.width(32)) _29 (.D(Write_Data), .en(and_30_out), .Q(_29_q), .clk(clock_1_out));  // open: clr
  Register #(.width(32)) _30 (.D(Write_Data), .en(and_31_out), .Q(_30_q), .clk(clock_1_out));  // open: clr
  Register #(.width(32)) _31 (.D(Write_Data), .en(and_32_out), .Q(_31_q), .clk(clock_1_out));  // open: clr
  Multiplexer #(.select(5), .width(32)) multiplexer_1 (
    .in0(_0_q), .in1(_1_q), .in2(_2_q), .in3(_3_q), .in4(_4_q), .in5(_5_q), .in6(_6_q), .in7(_7_q),
    .in8(_8_q), .in9(_9), .in10(_10_q), .in11(_11_q), .in12(_12_q), .in13(_13_q), .in14(_14_q), .in15(_15_q),
    .in16(_16_q), .in17(_17_q), .in18(_18_q), .in19(_19_q), .in20(_20_q), .in21(_21_q), .in22(_22_q),
    .in23(_23_q), .in24(t8), .in25(t9), .in26(_26_q), .in27(_27_q), .in28(_28_q), .in29(_29_q), .in30(_30_q),
    .in31(_31_q), .out(Read_Data_1), .sel(Read_Register1));  // open: en
  Multiplexer #(.select(5), .width(32)) multiplexer_2 (
    .in0(_0_q), .in1(_1_q), .in2(_2_q), .in3(_3_q), .in4(_4_q), .in5(_5_q), .in6(_6_q), .in7(_7_q),
    .in8(_8_q), .in9(_9), .in10(_10_q), .in11(_11_q), .in12(_12_q), .in13(_13_q), .in14(_14_q), .in15(_15_q),
    .in16(_16_q), .in17(_17_q), .in18(_18_q), .in19(_19_q), .in20(_20_q), .in21(_21_q), .in22(_22_q),
    .in23(_23_q), .in24(t8), .in25(t9), .in26(_26_q), .in27(_27_q), .in28(_28_q), .in29(_29_q), .in30(_30_q),
    .in31(_31_q), .out(Read_Data_2), .sel(Read_Register_2));  // open: en
endmodule

module Control_Unit__TO_DO (
  input  [5:0] OpCode,
  output RegDst,
  output Jump,
  output Branch,
  output RegWrt,
  output ALUSrc
);

  wire and_4_out, and_5_out, and_6_out, and_7_out, and_8_out, and_9_out, and_10_out, not_1_out, not_2_out,
       not_3_out, not_4_out, not_5_out, not_6_out, or_1_out, or_3_out, or_4_out;

  not not_1 (not_1_out, OpCode[0]);
  not not_2 (not_2_out, OpCode[2]);
  not not_3 (not_3_out, OpCode[4]);
  not not_4 (not_4_out, OpCode[3]);
  not not_5 (not_5_out, OpCode[5]);
  not not_6 (not_6_out, OpCode[1]);
  and and_1 (RegDst, not_5_out, not_3_out, not_4_out, not_2_out, not_6_out, not_1_out);
  and and_2 (Jump, not_4_out, not_2_out, OpCode[1], not_1_out);
  and and_3 (Branch, not_6_out, OpCode[2]);
  and and_4 (and_4_out, not_4_out, not_2_out, not_6_out, not_1_out);
  and and_5 (and_5_out, OpCode[3], OpCode[2], not_6_out);
  and and_6 (and_6_out, OpCode[3], not_6_out, not_1_out);
  and and_7 (and_7_out, OpCode[3], not_2_out, OpCode[1], not_1_out);
  and and_8 (and_8_out, OpCode[3], not_2_out, not_6_out);
  and and_9 (and_9_out, OpCode[3], OpCode[2], not_6_out);
  and and_10 (and_10_out, OpCode[3], not_3_out, OpCode[1], not_1_out);
  or or_1 (or_1_out, and_4_out, and_5_out);
  or or_2 (RegWrt, or_1_out, or_3_out);
  or or_3 (or_3_out, and_6_out, and_7_out);
  or or_4 (or_4_out, and_8_out, and_9_out);
  or or_5 (ALUSrc, or_4_out, and_10_out);
endmodule

module _1_Bit_ALU (
  input  Carry_In,
  input  A,
  input  AInvert,
  input  B,
  input  [1:0] Operation,
  input  Less,
  input  BInvert,
  output Result,
  output Set,
  output Carry_Out
);

  wire and_1_out, multiplexer_1_out, multiplexer_2_out, not_1_out, not_2_out, or_1_out;

  Multiplexer #(.enable("false")) multiplexer_1 (.in0(A), .in1(not_1_out), .out(multiplexer_1_out), .sel(AInvert));
  not not_1 (not_1_out, A);
  Multiplexer #(.enable("false")) multiplexer_2 (.in0(B), .in1(not_2_out), .out(multiplexer_2_out), .sel(BInvert));
  not not_2 (not_2_out, B);
  and and_1 (and_1_out, multiplexer_1_out, multiplexer_2_out);
  or or_1 (or_1_out, multiplexer_1_out, multiplexer_2_out);
  Adder #(.width(1)) adder_1 (
    .a(multiplexer_1_out), .b(multiplexer_2_out), .out(Set), .cin(Carry_In), .cout(Carry_Out));
  Multiplexer #(.select(2), .enable("false")) multiplexer_3 (
    .in0(and_1_out), .in1(or_1_out), .in2(Set), .in3(Less), .out(Result), .sel(Operation));
endmodule

module Shift_Left_2 (
  input  [31:0] Input,
  output [31:0] out_2
);

  Multiplier #(.width(32)) multiplier_1 (.a(Input), .b(32'h4), .out(out_2));  // open: cin, cout
endmodule

module Main_32_Bit_ALU (
  input  [3:0] Operation,
  input  [31:0] A,
  input  [4:0] Shamt,
  input  [31:0] B,
  input  [1:0] Shift_Operation,
  output Zero,
  output [31:0] Result
);

  wire [31:0] multiplexer_1_out, multiplexer_2_out, n32_bit_alu_to_do_1_main_result,
       shift_left_to_do_1_result, shift_right_to_do_1_result;

  Multiplexer #(.select(4), .width(32)) multiplexer_1 (
    .in0(A), .in1(A), .in2(A), .in3(A), .in4(A), .in5(A), .in6(B), .in7(B), .in8(A), .in9(A), .in10(A),
    .in11(A), .in12(A), .in13(A), .in14(A), .in15(A), .out(multiplexer_1_out), .sel(Operation));  // open: en
  Multiplexer #(.select(4), .width(32)) multiplexer_2 (
    .in0(B), .in1(B), .in2(B), .in3(B), .in4(B), .in5(B), .in6(A), .in7(A), .in8(B), .in9(B), .in10(B),
    .in11(B), .in12(B), .in13(B), .in14(B), .in15(B), .out(multiplexer_2_out), .sel(Operation));  // open: en
  _32_bit_ALU__TO_DO u_32_bit_alu_to_do_1 (
    .B(multiplexer_1_out), .A(multiplexer_2_out), .ALU_Operation(Operation), .Zero(Zero),
    .Main_Result(n32_bit_alu_to_do_1_main_result));  // open: OverFlow
  Shift_Left__TO_DO shift_left_to_do_1 (.Input(multiplexer_2_out), .Shifter(Shamt), .Result(shift_left_to_do_1_result));
  Shift_Right__TO_DO shift_right_to_do_1 (
    .Input(multiplexer_2_out), .Shifter(Shamt), .Result(shift_right_to_do_1_result));
  Multiplexer #(.select(2), .width(32)) multiplexer_3 (
    .in0(n32_bit_alu_to_do_1_main_result), .in2(shift_left_to_do_1_result), .in3(shift_right_to_do_1_result),
    .out(Result), .sel(Shift_Operation));  // open: in1, en
endmodule

module MainFunc (
  input  [31:0] Write__t9,
  input  Write_Signal,
  output [5:0] Opcode,
  output [3:0] Read_Data_2,
  output [31:0] Output_of_Address,
  output [31:0] t8,
  output [31:0] t9,
  output [31:0] _9
);

  wire and_1_out, bne_1_bne, clock_1_out, control_unit_to_do_1_alusrc, control_unit_to_do_1_branch,
       control_unit_to_do_1_jump, control_unit_to_do_1_regdst, control_unit_to_do_1_regwrt,
       main_32_bit_alu_1_zero, multiplexer_3_out, not_1_out;
  wire [1:0] shift_control_1_read_data_2;
  wire [3:0] alu_control_1_read_data_2, multiplexer_7_out, opcontrol_1_read_data_2;
  wire [4:0] multiplexer_1_out;
  wire [25:0] instruction_memory_to_do_1_out_2;
  wire [31:0] adder_1_out, adder_2_out, main_32_bit_alu_1_result, multiplexer_2_out, multiplexer_4_out,
       register_1_q, register_file_to_do_1_read_data_1, register_file_to_do_1_read_data_2,
       shift_left_2_1_out_2, shift_left_2_2_out_2, sign_extend_to_do_1_extended_bit;

  Register #(.width(32)) register_1 (
    .D(Output_of_Address), .en(1'b1), .Q(register_1_q), .clk(clock_1_out));  // open: clr
  Clock clock_1 (.out(clock_1_out));
  Instruction_Memory__TO_DO instruction_memory_to_do_1 (
    .Input(register_1_q[17:2]), .out_2({Opcode, instruction_memory_to_do_1_out_2}));
  Adder #(.width(32)) adder_1 (.a(register_1_q), .b(32'h4), .out(adder_1_out));  // open: cin, cout
  bne bne_1 (.In(Opcode), .bne(bne_1_bne));
  Shift_Left_2 shift_left_2_1 (.Input({Opcode, instruction_memory_to_do_1_out_2}), .out_2(shift_left_2_1_out_2));
  Control_Unit__TO_DO control_unit_to_do_1 (
    .OpCode(Opcode), .RegDst(control_unit_to_do_1_regdst), .Jump(control_unit_to_do_1_jump),
    .Branch(control_unit_to_do_1_branch), .RegWrt(control_unit_to_do_1_regwrt),
    .ALUSrc(control_unit_to_do_1_alusrc));
  Multiplexer #(.width(5)) multiplexer_1 (
    .in0(instruction_memory_to_do_1_out_2[20:16]), .in1(instruction_memory_to_do_1_out_2[15:11]),
    .out(multiplexer_1_out), .sel(control_unit_to_do_1_regdst));  // open: en
  Sign_Extend__TO_DO sign_extend_to_do_1 (
    .Input(instruction_memory_to_do_1_out_2[15:0]), .Extended_Bit(sign_extend_to_do_1_extended_bit));
  Shift_Left_2 shift_left_2_2 (.Input(sign_extend_to_do_1_extended_bit), .out_2(shift_left_2_2_out_2));
  Shift_Control shift_control_1 (
    .Funct(instruction_memory_to_do_1_out_2[5:0]), .Op(Opcode), .Read_Data_2(shift_control_1_read_data_2));
  ALU_Control alu_control_1 (.Funct(instruction_memory_to_do_1_out_2[5:0]), .Read_Data_2(alu_control_1_read_data_2));
  OpControl opcontrol_1 (.Op(Opcode), .Read_Data_2(opcontrol_1_read_data_2));
  Adder #(.width(32)) adder_2 (.a(shift_left_2_2_out_2), .b(adder_1_out), .out(adder_2_out));  // open: cin, cout
  and and_1 (and_1_out, control_unit_to_do_1_branch, multiplexer_3_out);
  Register_File__TO_DO register_file_to_do_1 (
    .RegWrite(control_unit_to_do_1_regwrt), .Read_Register1(instruction_memory_to_do_1_out_2[25:21]),
    .Read_Register_2(instruction_memory_to_do_1_out_2[20:16]), .Write_Register(multiplexer_1_out),
    .Write_Data(main_32_bit_alu_1_result), .Write_to__t9(Write__t9), .Write_Signal(Write_Signal),
    .Read_Data_1(register_file_to_do_1_read_data_1), .Read_Data_2(register_file_to_do_1_read_data_2),
    ._9(_9), .t8(t8), .t9(t9));
  Multiplexer #(.width(32)) multiplexer_2 (
    .in0(adder_1_out), .in1(adder_2_out), .out(multiplexer_2_out), .sel(and_1_out));  // open: en
  Multiplexer multiplexer_3 (
    .in0(main_32_bit_alu_1_zero), .in1(not_1_out), .out(multiplexer_3_out), .sel(bne_1_bne));  // open: en
  Multiplexer #(.width(32)) multiplexer_4 (
    .in0(register_file_to_do_1_read_data_2), .in1(sign_extend_to_do_1_extended_bit), .out(multiplexer_4_out),
    .sel(control_unit_to_do_1_alusrc));  // open: en
  Multiplexer #(.width(32)) multiplexer_5 (
    .in0(multiplexer_2_out), .in1({adder_1_out[31:22], shift_left_2_1_out_2[21:0]}), .out(Output_of_Address),
    .sel(control_unit_to_do_1_jump));  // open: en
  not not_1 (not_1_out, main_32_bit_alu_1_zero);
  Main_32_Bit_ALU main_32_bit_alu_1 (
    .A(register_file_to_do_1_read_data_1), .Shamt(instruction_memory_to_do_1_out_2[10:6]),
    .B(multiplexer_4_out), .Operation(Read_Data_2), .Shift_Operation(shift_control_1_read_data_2),
    .Zero(main_32_bit_alu_1_zero), .Result(main_32_bit_alu_1_result));
  Multiplexer #(.width(4)) multiplexer_6 (
    .in0(multiplexer_7_out), .in1(opcontrol_1_read_data_2), .out(Read_Data_2),
    .sel(control_unit_to_do_1_branch));  // open: en
  Multiplexer #(.width(4)) multiplexer_7 (
    .in0(alu_control_1_read_data_2), .in1(opcontrol_1_read_data_2), .out(multiplexer_7_out),
    .sel(control_unit_to_do_1_alusrc));  // open: en
endmodule

module ALU_Control (
  input  [5:0] Funct,
  output [3:0] Read_Data_2
);

  wire and_2_out, and_3_out, and_4_out, and_5_out, and_6_out, and_7_out, not_1_out, not_2_out, not_3_out,
       not_4_out, not_5_out, not_6_out;

  not not_1 (not_1_out, Funct[1]);
  not not_2 (not_2_out, Funct[4]);
  not not_3 (not_3_out, Funct[5]);
  not not_4 (not_4_out, Funct[3]);
  not not_5 (not_5_out, Funct[2]);
  not not_6 (not_6_out, Funct[0]);
  and and_1 (Read_Data_2[3], Funct[5], not_2_out, not_4_out, Funct[2], Funct[1], Funct[0]);
  and and_2 (and_2_out, not_2_out, not_5_out, Funct[1], not_6_out);
  and and_3 (and_3_out, Funct[5], not_2_out, not_4_out, Funct[2], Funct[1], Funct[0]);
  and and_4 (and_4_out, Funct[5], not_2_out, not_5_out, Funct[1], not_6_out);
  and and_5 (and_5_out, Funct[5], not_2_out, not_4_out, not_5_out, not_1_out, not_6_out);
  and and_6 (and_6_out, Funct[5], not_2_out, Funct[3], not_5_out, Funct[1], not_6_out);
  and and_7 (and_7_out, Funct[5], not_2_out, not_4_out, Funct[2], not_1_out, Funct[0]);
  or or_1 (Read_Data_2[2], and_2_out, and_3_out);
  or or_2 (Read_Data_2[1], and_4_out, and_5_out);
  or or_3 (Read_Data_2[0], and_6_out, and_7_out);
endmodule

module Shift_Control (
  input  [5:0] Funct,
  input  [5:0] Op,
  output [1:0] Read_Data_2
);

  wire and_1_out, and_2_out, and_3_out, not_1_out, not_2_out, not_3_out, not_4_out, not_5_out, not_6_out,
       not_7_out, not_8_out, not_9_out, not_10_out, not_11_out, not_12_out;

  not not_1 (not_1_out, Funct[4]);
  not not_2 (not_2_out, Funct[5]);
  not not_3 (not_3_out, Op[0]);
  not not_4 (not_4_out, Op[1]);
  not not_5 (not_5_out, Funct[1]);
  not not_6 (not_6_out, Funct[2]);
  not not_7 (not_7_out, Funct[3]);
  not not_8 (not_8_out, Funct[0]);
  not not_9 (not_9_out, Op[5]);
  not not_10 (not_10_out, Op[4]);
  not not_11 (not_11_out, Op[3]);
  not not_12 (not_12_out, Op[2]);
  and and_1 (and_1_out, not_8_out, not_6_out, not_7_out, not_1_out, not_2_out);
  and and_2 (and_2_out, not_2_out, not_1_out, not_7_out, not_6_out, Funct[1], not_8_out);
  and and_3 (and_3_out, not_9_out, not_10_out, not_11_out, not_12_out, not_4_out, not_3_out);
  and and_4 (Read_Data_2[1], and_1_out, and_3_out);
  and and_5 (Read_Data_2[0], and_2_out, and_3_out);
endmodule

module PC (
  input  [31:0] Funct,
  output [31:0] Read_Data_2
);


  assign Read_Data_2 = Funct;
endmodule

module practiceri (
  input  Funct,
  input  [4:0] Funct_2,
  input  [4:0] Funct_3,
  input  [4:0] Funct_4,
  input  [31:0] Funct_5,
  input  [31:0] Funct_6,
  input  Funct_7,
  output [31:0] Read_Data_2
);

  Register_File__TO_DO register_file_to_do_1 (
    .RegWrite(Funct), .Read_Register1(Funct_2), .Read_Register_2(Funct_3), .Write_Register(Funct_4),
    .Write_Data(Funct_5), .Write_to__t9(Funct_6), .Write_Signal(Funct_7), .t8(Read_Data_2));  // open: Read_Data_1, Read_Data_2, _9, t9
endmodule

module OpControl (
  input  [5:0] Op,
  output [3:0] Read_Data_2
);

  wire and_2_out, and_3_out, and_4_out, and_5_out, and_6_out, and_7_out, and_8_out, and_9_out, and_10_out,
       and_11_out, not_1_out, not_2_out, not_3_out, not_4_out;

  not not_1 (not_1_out, Op[3]);
  not not_2 (not_2_out, Op[1]);
  not not_3 (not_3_out, Op[0]);
  not not_4 (not_4_out, Op[2]);
  and and_1 (Read_Data_2[3], not_1_out, not_4_out, not_2_out, not_3_out);
  and and_2 (and_2_out, not_2_out, not_1_out, not_3_out);
  and and_3 (and_3_out, not_1_out, Op[2], not_2_out);
  and and_4 (and_4_out, Op[3], not_4_out, Op[1], not_3_out);
  and and_5 (and_5_out, not_1_out, not_2_out, not_3_out);
  and and_6 (and_6_out, not_1_out, Op[2], not_2_out);
  and and_7 (and_7_out, Op[3], not_4_out, not_2_out, not_3_out);
  and and_8 (and_8_out, Op[3], not_4_out, Op[1], not_3_out);
  and and_9 (and_9_out, not_1_out, not_4_out, not_2_out, not_3_out);
  and and_10 (and_10_out, Op[3], Op[2], not_2_out, Op[0]);
  and and_11 (and_11_out, Op[3], not_4_out, Op[1], not_3_out);
  or or_1 (Read_Data_2[2], and_2_out, and_3_out, and_4_out);
  or or_2 (Read_Data_2[1], and_5_out, and_6_out, and_7_out, and_8_out);
  or or_3 (Read_Data_2[0], and_9_out, and_10_out, and_11_out);
endmodule

module bne (
  input  [5:0] In,
  output bne
);

  wire not_1_out, not_2_out, not_5_out, not_6_out;

  not not_1 (not_1_out, In[5]);
  not not_2 (not_2_out, In[3]);
  // NOT_Gate not_3 has open pins: in=In[0], out=open
  // NOT_Gate not_4 has open pins: in=In[2], out=open
  not not_5 (not_5_out, In[4]);
  not not_6 (not_6_out, In[1]);
  and and_1 (bne, In[2], In[0], not_1_out, not_5_out, not_2_out, not_6_out);
endmodule
